# Fritzing sketch diagram (saved by Fritzing 0.9.2b)
breadboards: 1

parts:
  part = Arduino Uno (Rev3) - ICSP
  S1 = SWITCH-MOMENTARY-2 [package=tactile-pth-12mm]
  J1 = Basic Servo
  5V = Battery Holders [package=battery-aa]

nets:
  GND: part.GND, J1.gnd, 5V.-
  N1: part.D5_PWM, J1.pulse
  N2: part.D6_PWM, S1.1
  VIN: part.VIN, J1.vcc, 5V.+
